// Logisim project convolutional_code_communication.circ as structural Verilog: 12 circuits, main circuit main
module main (
  input  in_1,
  input  in_2,
  input  in_3,
  input  in_4,
  input  in_5
);

  wire Clk_out, convolutional_encoder_1_clk_out, convolutional_encoder_1_serial_out,
       noise_generator_1_noisy_serial_out, Reset_out, sipo12_1_q0, sipo12_1_q1, sipo12_1_q2, sipo12_1_q3,
       sipo12_1_q4, sipo12_1_q5, sipo12_1_q6, sipo12_1_q7, sipo12_1_q8, sipo12_1_q9, sipo12_1_q10,
       sipo12_1_q11;

  Button Clk (.out(Clk_out));
  Button Reset (.out(Reset_out));
  LED led_1 (.in(convolutional_encoder_1_serial_out));
  Convolutional_encoder convolutional_encoder_1 (
    .M3(in_1), .M2(in_2), .M1(in_3), .M0(in_4), .EN(in_5), .reset(Reset_out), .clk(Clk_out),
    .Serial_out(convolutional_encoder_1_serial_out), .clk_out(convolutional_encoder_1_clk_out));
  LED led_2 (.in(noise_generator_1_noisy_serial_out));
  Noise_generator noise_generator_1 (
    .Serial_in(convolutional_encoder_1_serial_out), .reset(Reset_out),
    .clk_in(convolutional_encoder_1_clk_out), .Noisy_serial_out(noise_generator_1_noisy_serial_out));
  LED led_3 (.in(sipo12_1_q11));
  SIPO12 sipo12_1 (
    .serial_input(noise_generator_1_noisy_serial_out), .clk(convolutional_encoder_1_clk_out),
    .reset(Reset_out), .q11(sipo12_1_q11), .q10(sipo12_1_q10), .q9(sipo12_1_q9), .q8(sipo12_1_q8),
    .q7(sipo12_1_q7), .q6(sipo12_1_q6), .q5(sipo12_1_q5), .q4(sipo12_1_q4), .q3(sipo12_1_q3),
    .q2(sipo12_1_q2), .q1(sipo12_1_q1), .q0(sipo12_1_q0));
  LED led_4 (.in(sipo12_1_q10));
  LED led_5 (.in(sipo12_1_q9));
  LED led_6 (.in(sipo12_1_q8));
  LED led_7 (.in(sipo12_1_q7));
  LED led_8 (.in(sipo12_1_q6));
  LED led_9 (.in(sipo12_1_q5));
  LED led_10 (.in(sipo12_1_q4));
  LED led_11 (.in(sipo12_1_q3));
  LED led_12 (.in(sipo12_1_q2));
  LED led_13 (.in(sipo12_1_q1));
  LED led_14 (.in(sipo12_1_q0));
endmodule

module PISO_input (
  input  M3,
  input  M2,
  input  M1,
  input  M0,
  input  reset,
  input  EN,
  input  clk,
  output serial_out,
  output clk_out_2f,
  output clk_out
);

  wire and_1_out, and_2_out, and_3_out, and_5_out, and_6_out, and_7_out, and_8_out, d_ff_1_q, d_ff_1_qn,
       d_ff_2_q, F1_q, F3_q, nor_1_out, not_1_out, or_2_out, or_3_out, or_4_out;

  not not_1 (not_1_out, EN);
  D_Flip_Flop d_ff_1 (.D(d_ff_1_qn), .clk(clk_out), .Q(d_ff_1_q), .Qn(d_ff_1_qn), .reset(reset));  // open: preset
  and and_1 (and_1_out, not_1_out, M3);
  or or_1 (clk_out_2f, nor_1_out, d_ff_1_q);
  and and_2 (and_2_out, EN, F1_q);
  D_Flip_Flop F1 (.D(and_1_out), .clk(clk_out_2f), .Q(F1_q));  // open: Qn, preset, reset
  and and_3 (and_3_out, M2, not_1_out);
  or or_2 (or_2_out, and_2_out, and_3_out);
  and and_4 (clk_out, EN, clk);
  nor nor_1 (nor_1_out, EN, clk);
  D_Flip_Flop F3 (.D(or_2_out), .clk(clk_out_2f), .Q(F3_q), .reset(reset));  // open: Qn, preset
  and and_5 (and_5_out, M1, not_1_out);
  and and_6 (and_6_out, EN, F3_q);
  or or_3 (or_3_out, and_6_out, and_5_out);
  D_Flip_Flop d_ff_2 (.D(or_3_out), .clk(clk_out_2f), .Q(d_ff_2_q), .reset(reset));  // open: Qn, preset
  and and_7 (and_7_out, M0, not_1_out);
  and and_8 (and_8_out, EN, d_ff_2_q);
  or or_4 (or_4_out, and_8_out, and_7_out);
  D_Flip_Flop d_ff_3 (.D(or_4_out), .clk(clk_out_2f), .Q(serial_out), .reset(reset));  // open: Qn, preset
endmodule

module parity_generation (
  input  serial_in,
  input  clk_in_2f,
  input  reset,
  input  EN,
  input  clk,
  output S_out,
  output clk_out
);

  wire and_1_out, and_2_out, d_ff_1_q, d_ff_2_q, d_ff_3_q, j_k_ff_1_q, j_k_ff_1_qn, not_1_out, xor_1_out,
       xor_2_out, xor_3_out, xor_4_out;

  D_Flip_Flop d_ff_1 (.D(serial_in), .clk(clk_in_2f), .Q(d_ff_1_q), .reset(reset));  // open: Qn, preset
  D_Flip_Flop d_ff_2 (.D(d_ff_1_q), .clk(clk_in_2f), .Q(d_ff_2_q), .reset(reset));  // open: Qn, preset
  not not_1 (not_1_out, reset);
  xor xor_1 (xor_1_out, not_1_out, EN);
  xor xor_2 (xor_2_out, d_ff_1_q, d_ff_3_q);
  D_Flip_Flop d_ff_3 (.D(d_ff_2_q), .clk(clk_in_2f), .Q(d_ff_3_q), .reset(reset));  // open: Qn, preset
  xor xor_3 (xor_3_out, d_ff_3_q, d_ff_2_q);
  J_K_Flip_Flop j_k_ff_1 (
    .J(1'b1), .K(1'b1), .clk(clk), .Q(j_k_ff_1_q), .Qn(j_k_ff_1_qn), .reset(xor_1_out));  // open: preset
  xor xor_4 (xor_4_out, xor_3_out, d_ff_1_q);
  and and_1 (and_1_out, xor_2_out, j_k_ff_1_qn);
  and and_2 (and_2_out, xor_4_out, j_k_ff_1_q);
  or or_1 (S_out, and_1_out, and_2_out);

  assign clk_out = clk;
endmodule

module J_logic (
  input  Q0,
  input  Q1,
  input  Q2,
  input  Q3,
  output J0,
  output J1,
  output J2,
  output J3
);

  wire and_1_out, and_2_out, and_3_out, and_4_out, and_5_out, and_6_out, and_7_out, and_8_out, and_9_out,
       not_1_out, not_2_out, not_3_out, not_4_out, or_1_out;

  not not_1 (not_1_out, Q0);
  not not_2 (not_2_out, Q1);
  not not_3 (not_3_out, Q2);
  not not_4 (not_4_out, Q3);
  and and_1 (and_1_out, Q2, not_1_out);
  and and_2 (and_2_out, not_4_out, not_2_out, not_1_out);
  or or_1 (or_1_out, Q2, Q3);
  and and_3 (and_3_out, not_4_out, not_3_out, Q1);
  and and_4 (and_4_out, Q1, not_1_out);
  and and_5 (and_5_out, or_1_out, not_2_out);
  and and_6 (and_6_out, Q0, not_3_out);
  and and_7 (and_7_out, Q0, Q1, not_3_out);
  and and_8 (and_8_out, Q1, Q2, not_1_out);
  or or_2 (J0, and_5_out, and_3_out);
  or or_3 (J1, Q3, and_6_out, and_1_out);
  and and_9 (and_9_out, Q3, Q1);
  or or_4 (J3, and_7_out, and_8_out);
  or or_5 (J2, and_4_out, and_9_out, and_2_out);
endmodule

module K_logic (
  input  Q0,
  input  Q1,
  input  Q2,
  input  Q3,
  output K0,
  output K1,
  output K2,
  output K3
);

  wire and_1_out, and_2_out, and_3_out, not_2_out, not_3_out, not_4_out;

  // NOT_Gate not_1 has open pins: in=Q0, out=open
  not not_2 (not_2_out, Q1);
  not not_3 (not_3_out, Q2);
  not not_4 (not_4_out, Q3);
  and and_1 (and_1_out, not_4_out, not_3_out, not_2_out);
  and and_2 (and_2_out, Q3, not_2_out);
  or or_1 (K1, Q0, Q2);
  and and_3 (and_3_out, Q2, Q1, not_4_out);
  or or_2 (K0, and_2_out, and_3_out, and_1_out);

  assign K2 = 1'b1;
  assign K3 = Q1;
endmodule

module pseudo_noise_seq_counter (
  input  clk,
  input  Reset,
  output Q0,
  output Q1,
  output Q2,
  output Q3
);

  wire j_logic_1_j0, j_logic_1_j1, j_logic_1_j2, j_logic_1_j3, k_logic_1_k0, k_logic_1_k1, k_logic_1_k2,
       k_logic_1_k3;

  J_K_Flip_Flop JK0 (.J(j_logic_1_j0), .K(k_logic_1_k0), .clk(clk), .Q(Q0), .reset(Reset));  // open: Qn, preset
  J_K_Flip_Flop JK1 (.J(j_logic_1_j1), .K(k_logic_1_k1), .clk(clk), .Q(Q1), .reset(Reset));  // open: Qn, preset
  J_K_Flip_Flop JK2 (.J(j_logic_1_j2), .K(k_logic_1_k2), .clk(clk), .Q(Q2), .reset(Reset));  // open: Qn, preset
  J_K_Flip_Flop JK3 (.J(j_logic_1_j3), .K(k_logic_1_k3), .clk(clk), .Q(Q3), .preset(Reset));  // open: Qn, reset
  K_logic k_logic_1 (
    .Q0(Q0), .Q1(Q1), .Q2(Q2), .Q3(Q3), .K0(k_logic_1_k0), .K1(k_logic_1_k1), .K2(k_logic_1_k2),
    .K3(k_logic_1_k3));
  J_logic j_logic_1 (
    .Q0(Q0), .Q1(Q1), .Q2(Q2), .Q3(Q3), .J0(j_logic_1_j0), .J1(j_logic_1_j1), .J2(j_logic_1_j2),
    .J3(j_logic_1_j3));
endmodule

module mod12_counter (
  input  clk_in,
  input  reset,
  output C0,
  output C1,
  output C2,
  output C3
);

  wire and_1_out, and_2_out, and_3_out, JK0_q, JK0_qn, JK1_q, JK2_q, JK3_q, JK3_qn;

  J_K_Flip_Flop JK0 (.J(JK0_qn), .K(JK0_q), .clk(clk_in), .Q(JK0_q), .Qn(JK0_qn), .reset(reset));  // open: preset
  J_K_Flip_Flop JK1 (.J(JK0_q), .K(JK0_q), .clk(clk_in), .Q(JK1_q), .reset(reset));  // open: Qn, preset
  J_K_Flip_Flop JK2 (.J(and_2_out), .K(and_3_out), .clk(clk_in), .Q(JK2_q), .reset(reset));  // open: Qn, preset
  J_K_Flip_Flop JK3 (
    .J(and_1_out), .K(and_3_out), .clk(clk_in), .Q(JK3_q), .Qn(JK3_qn), .reset(reset));  // open: preset
  and and_1 (and_1_out, JK1_q, JK0_q, JK2_q);
  and and_2 (and_2_out, JK1_q, JK0_q, JK3_qn);
  and and_3 (and_3_out, JK1_q, JK0_q);
  D_Flip_Flop d_ff_1 (.D(JK0_q), .clk(clk_in), .Q(C0), .reset(reset));  // open: Qn, preset
  D_Flip_Flop d_ff_2 (.D(JK1_q), .clk(clk_in), .Q(C1), .reset(reset));  // open: Qn, preset
  D_Flip_Flop d_ff_3 (.D(JK2_q), .clk(clk_in), .Q(C2), .reset(reset));  // open: Qn, preset
  D_Flip_Flop d_ff_4 (.D(JK3_q), .clk(clk_in), .Q(C3), .reset(reset));  // open: Qn, preset
endmodule

module clk_12_1 (
  input  clk_in,
  input  reset,
  output clk_counter
);

  wire and_1_out, and_2_out, and_3_out, and_4_out, and_5_out, j_k_ff_1_q, JK0_q, JK0_qn, JK1_q, JK1_qn,
       JK2_q, JK2_qn, JK3_q, JK3_qn;

  J_K_Flip_Flop JK0 (.J(JK0_qn), .K(JK0_q), .clk(clk_in), .Q(JK0_q), .Qn(JK0_qn), .reset(reset));  // open: preset
  J_K_Flip_Flop JK1 (.J(JK0_q), .K(JK0_q), .clk(clk_in), .Q(JK1_q), .Qn(JK1_qn), .reset(reset));  // open: preset
  J_K_Flip_Flop JK2 (
    .J(and_2_out), .K(and_3_out), .clk(clk_in), .Q(JK2_q), .Qn(JK2_qn), .reset(reset));  // open: preset
  J_K_Flip_Flop JK3 (
    .J(and_1_out), .K(and_3_out), .clk(clk_in), .Q(JK3_q), .Qn(JK3_qn), .reset(reset));  // open: preset
  and and_1 (and_1_out, JK1_q, JK0_q, JK2_q);
  and and_2 (and_2_out, JK1_q, JK0_q, JK3_qn);
  and and_3 (and_3_out, JK1_q, JK0_q);
  and and_4 (and_4_out, JK0_qn, JK2_qn, JK3_qn, JK1_qn);
  and and_5 (and_5_out, JK3_q, JK2_qn, JK1_q, JK0_q);
  J_K_Flip_Flop j_k_ff_1 (
    .J(and_5_out), .K(and_4_out), .clk(clk_in), .Q(j_k_ff_1_q), .reset(reset));  // open: Qn, preset
  D_Flip_Flop d_ff_1 (.D(j_k_ff_1_q), .clk(clk_in), .Q(clk_counter), .reset(reset));  // open: Qn, preset
endmodule

module equality_check (
  input  C0,
  input  C1,
  input  C2,
  input  C3,
  input  Q0,
  input  Q1,
  input  Q2,
  input  Q3,
  output equality_bit
);

  wire and_1_out, and_2_out, xnor_1_out, xnor_2_out, xnor_3_out, xnor_4_out;

  xnor xnor_1 (xnor_1_out, C0, Q0);
  xnor xnor_2 (xnor_2_out, C1, Q1);
  xnor xnor_3 (xnor_3_out, C2, Q2);
  xnor xnor_4 (xnor_4_out, C3, Q3);
  and and_1 (and_1_out, xnor_1_out, xnor_2_out);
  and and_2 (and_2_out, xnor_3_out, xnor_4_out);
  and and_3 (equality_bit, and_1_out, and_2_out);
endmodule

module Noise_generator (
  input  Serial_in,
  input  reset,
  input  clk_in,
  output Noisy_serial_out
);

  wire and_1_out, and_2_out, clk_12_1_1_clk_counter, equality_check_1_equality_bit, mod12_counter_1_c0,
       mod12_counter_1_c1, mod12_counter_1_c2, mod12_counter_1_c3, not_1_out, not_2_out,
       pseudo_noise_seq_counter_1_q0, pseudo_noise_seq_counter_1_q1, pseudo_noise_seq_counter_1_q2,
       pseudo_noise_seq_counter_1_q3;

  clk_12_1 clk_12_1_1 (.clk_in(clk_in), .reset(reset), .clk_counter(clk_12_1_1_clk_counter));
  mod12_counter mod12_counter_1 (
    .clk_in(clk_in), .reset(reset), .C0(mod12_counter_1_c0), .C1(mod12_counter_1_c1),
    .C2(mod12_counter_1_c2), .C3(mod12_counter_1_c3));
  pseudo_noise_seq_counter pseudo_noise_seq_counter_1 (
    .clk(clk_12_1_1_clk_counter), .Reset(reset), .Q0(pseudo_noise_seq_counter_1_q0),
    .Q1(pseudo_noise_seq_counter_1_q1), .Q2(pseudo_noise_seq_counter_1_q2), .Q3(pseudo_noise_seq_counter_1_q3));
  LED led_1 (.in(equality_check_1_equality_bit));
  equality_check equality_check_1 (
    .C0(mod12_counter_1_c0), .C1(mod12_counter_1_c1), .C2(mod12_counter_1_c2), .C3(mod12_counter_1_c3),
    .Q0(pseudo_noise_seq_counter_1_q0), .Q1(pseudo_noise_seq_counter_1_q1),
    .Q2(pseudo_noise_seq_counter_1_q2), .Q3(pseudo_noise_seq_counter_1_q3),
    .equality_bit(equality_check_1_equality_bit));
  not not_1 (not_1_out, Serial_in);
  not not_2 (not_2_out, equality_check_1_equality_bit);
  and and_1 (and_1_out, not_2_out, Serial_in);
  and and_2 (and_2_out, equality_check_1_equality_bit, not_1_out);
  or or_1 (Noisy_serial_out, and_1_out, and_2_out);
endmodule

module Convolutional_encoder (
  input  M3,
  input  M2,
  input  M1,
  input  M0,
  input  EN,
  input  reset,
  input  clk,
  output Serial_out,
  output clk_out
);

  wire piso_input_1_clk_out, piso_input_1_clk_out_2f, piso_input_1_serial_out;

  PISO_input piso_input_1 (
    .M3(M3), .M2(M2), .M1(M1), .M0(M0), .reset(reset), .EN(EN), .clk(clk),
    .serial_out(piso_input_1_serial_out), .clk_out_2f(piso_input_1_clk_out_2f), .clk_out(piso_input_1_clk_out));
  parity_generation parity_generation_1 (
    .serial_in(piso_input_1_serial_out), .clk_in_2f(piso_input_1_clk_out_2f), .reset(reset), .EN(EN),
    .clk(piso_input_1_clk_out), .S_out(Serial_out), .clk_out(clk_out));
endmodule

module SIPO12 (
  input  serial_input,
  input  clk,
  input  reset,
  output q11,
  output q10,
  output q9,
  output q8,
  output q7,
  output q6,
  output q5,
  output q4,
  output q3,
  output q2,
  output q1,
  output q0
);

  D_Flip_Flop d_ff_1 (.D(serial_input), .clk(clk), .Q(q10), .reset(reset));  // open: Qn, preset
  D_Flip_Flop d_ff_2 (.D(q10), .clk(clk), .Q(q9), .reset(reset));  // open: Qn, preset
  D_Flip_Flop d_ff_3 (.D(q9), .clk(clk), .Q(q8), .reset(reset));  // open: Qn, preset
  D_Flip_Flop d_ff_4 (.D(q8), .clk(clk), .Q(q7), .reset(reset));  // open: Qn, preset
  D_Flip_Flop d_ff_5 (.D(q7), .clk(clk), .Q(q6), .reset(reset));  // open: Qn, preset
  D_Flip_Flop d_ff_6 (.D(q6), .clk(clk), .Q(q5), .reset(reset));  // open: Qn, preset
  D_Flip_Flop d_ff_7 (.D(q5), .clk(clk), .Q(q4), .reset(reset));  // open: Qn, preset
  D_Flip_Flop d_ff_8 (.D(q4), .clk(clk), .Q(q3), .reset(reset));  // open: Qn, preset
  D_Flip_Flop d_ff_9 (.D(q3), .clk(clk), .Q(q2), .reset(reset));  // open: Qn, preset
  D_Flip_Flop d_ff_10 (.D(q2), .clk(clk), .Q(q1), .reset(reset));  // open: Qn, preset
  D_Flip_Flop d_ff_11 (.D(q1), .clk(clk), .Q(q0), .reset(reset));  // open: Qn, preset

  assign q11 = serial_input;
endmodule
